// Digital circuit ALU.dig as structural Verilog
module ALU (
  input  [31:0] A,
  input  [31:0] B,
  input  [4:0] alu_op,
  output [31:0] out
);

  wire [0:0] slt, sltu;
  wire [31:0] add, \and , div, divu, mult, multh, multhu, multiplexer_1_out, multiplexer_2_out, multu, \or ,
       rem, remu, sll, sra, srl, sub, \xor ;

  assign \and  = A & B;  // And and_1, 32 bits wide
  assign \or  = A | B;  // Or or_1, 32 bits wide
  assign \xor  = A ^ B;  // XOr xor_1, 32 bits wide
  Add #(.Bits(32)) adder (.a(A), .b(B), .c_i(1'b0), .s(add));  // open: c_o
  Sub #(.Bits(32)) subtracter (.a(A), .b(B), .c_i(1'b0), .s(sub));  // open: c_o
  Mul #(.Signed("true"), .Bits(32)) mul_1 (.a(A), .b(B), .mul({multh, mult}));
  Div #(.Signed("true"), .Bits(32)) div_1 (.a(A), .b(B), .q(div), .r(rem));
  Mul #(.Bits(32)) mul_2 (.a(A), .b(B), .mul({multhu, multu}));
  Div #(.Bits(32)) div_2 (.a(A), .b(B), .q(divu), .r(remu));
  BarrelShifter #(.Bits(32)) u_sll (.in(A), .shift({1'b0, B[4:0]}), .out(sll));
  BarrelShifter #(.Bits(32), .direction("right")) u_srl (.in(A), .shift({1'b0, B[4:0]}), .out(srl));
  BarrelShifter #(.Bits(32), .barrelShifterMode("arithmetic"), .barrelSigned("true"), .direction("right")) u_sra (
    .in(A), .shift({2'b00, B[4:0]}), .out(sra));
  Comparator #(.Signed("true"), .Bits(32)) u_slt (.a(A), .b(B), .lt(slt[0]));  // open: gt, eq
  Comparator #(.Bits(32)) u_sltu (.a(A), .b(B), .lt(sltu[0]));  // open: gt, eq
  Multiplexer #(.Bits(32)) multiplexer_1 (.sel(alu_op[3]), .in_0(add), .in_1(sub), .out(multiplexer_1_out));
  Multiplexer #(.Bits(32)) multiplexer_2 (.sel(alu_op[3]), .in_0(srl), .in_1(sra), .out(multiplexer_2_out));
  Multiplexer #(.Selector_Bits(4), .Bits(32)) multiplexer_3 (
    .sel({alu_op[4], alu_op[2:0]}), .in_0(multiplexer_1_out), .in_1(sll), .in_2({{31{1'b0}}, slt[0]}),
    .in_3({{31{1'b0}}, sltu[0]}), .in_4(\xor ), .in_5(multiplexer_2_out), .in_6(\or ), .in_7(\and ),
    .in_8(mult), .in_9(multh), .in_10({32{1'b0}}), .in_11(multhu), .in_12(div), .in_13(divu), .in_14(rem),
    .in_15(remu), .out(out));

  // Other names for the same wires on the sheet: f3[2:0] = alu_op[2:0]; sel[3:0] = {alu_op[4], alu_op[2:0]};
  //   f9 = alu_op[3]

  // Notes on the sheet:
  //   A: default 8
  //   B: default 7
endmodule
