// Digital circuit BType.dig as structural Verilog
module BType (
  input  [24:0] inst,
  output [31:0] imm32
);

  // Probe on inst
  BitExtender #(.inputBits(13), .outputBits(32)) bitextender_1 (
    .in({inst[24], inst[0], inst[23:18], inst[4:1], 1'b0}), .out(imm32));
  // Probe on {inst[24], inst[0], inst[23:18], inst[4:1], 1'b0}
  // Probe on imm32
endmodule
