// Digital circuit Branch.dig as structural Verilog
module Branch (
  input  [31:0] rs1,
  input  [31:0] rs2,
  input  [3:0] BrOp,
  output out
);

  wire eq, equ, gr, gru, less, lessu, multiplexer_1_out, multiplexer_2_out, multiplexer_3_out,
       multiplexer_4_out, not_1_out, notconnected_1_out, or_1_out;

  // Probe on BrOp[2:0]
  // Probe on BrOp[3]
  Comparator #(.Signed("true"), .Bits(32)) comparator_1 (.a(rs1), .b(rs2), .gt(gr), .eq(eq), .lt(less));
  Comparator #(.Bits(32)) comparator_2 (.a(rs1), .b(rs2), .gt(gru), .eq(equ), .lt(lessu));
  Multiplexer multiplexer_1 (.sel(BrOp[1]), .in_0(eq), .in_1(equ), .out(multiplexer_1_out));
  Multiplexer multiplexer_2 (.sel(BrOp[1]), .in_0(gr), .in_1(gru), .out(multiplexer_2_out));
  Multiplexer multiplexer_3 (.sel(BrOp[1]), .in_0(less), .in_1(lessu), .out(multiplexer_3_out));
  or or_1 (or_1_out, multiplexer_1_out, multiplexer_2_out);
  not not_1 (not_1_out, eq);
  Multiplexer #(.Selector_Bits(3)) multiplexer_4 (
    .sel(BrOp[2:0]), .in_0(eq), .in_1(not_1_out), .in_2(notconnected_1_out), .in_3(notconnected_1_out),
    .in_4(multiplexer_3_out), .in_5(or_1_out), .in_6(multiplexer_3_out), .in_7(or_1_out),
    .out(multiplexer_4_out));
  // NotConnected on notconnected_1_out
  // Probe on or_1_out
  Multiplexer multiplexer_5 (.sel(BrOp[3]), .in_0(multiplexer_4_out), .in_1(1'b1), .out(out));

  // Other names for the same wires on the sheet: funct3[2:0] = BrOp[2:0]; bu = BrOp[1]; j = BrOp[3]
endmodule
