// Digital circuit Externsor.dig as structural Verilog
module Externsor (
  input  [11:0] imm,
  output [31:0] imm32
);

  BitExtender #(.inputBits(12), .outputBits(32)) bitextender_1 (.in(imm), .out(imm32));
endmodule
