// Digital circuit IType.dig as structural Verilog
module IType (
  input  [24:0] inst,
  output [31:0] imm32
);

  BitExtender #(.inputBits(12), .outputBits(32)) bitextender_1 (.in(inst[24:13]), .out(imm32));
  // Probe on inst[24:13]
  // Probe on imm32
endmodule
