// Digital circuit ImmGenerator.dig as structural Verilog
module ImmGenerator (
  input  [24:0] inst,
  input  [2:0] ImmOp,
  output [31:0] imm
);

  wire [31:0] btype_1_imm32, itype_1_imm32, jtype_1_imm32, notconnected_1_out, stype_1_imm32, utype_1_imm32;

  IType itype_1 (.inst(inst), .imm32(itype_1_imm32));
  BType btype_1 (.inst(inst), .imm32(btype_1_imm32));
  JType jtype_1 (.inst(inst), .imm32(jtype_1_imm32));
  SType stype_1 (.inst(inst), .imm32(stype_1_imm32));
  UType utype_1 (.inst(inst), .imm32(utype_1_imm32));
  Multiplexer #(.Bits(32), .Selector_Bits(3)) multiplexer_1 (
    .sel(ImmOp), .in_0(notconnected_1_out), .in_1(itype_1_imm32), .in_2(stype_1_imm32), .in_3(btype_1_imm32),
    .in_4(utype_1_imm32), .in_5(notconnected_1_out), .in_6(notconnected_1_out), .in_7(jtype_1_imm32),
    .out(imm));
  // NotConnected on notconnected_1_out
endmodule
