// Digital circuit Insts Memory.dig as structural Verilog
module Insts_Memory (
  input  [31:0] pc,
  output [31:0] out
);

  wire [23:0] SUM_2_s, SUM_3_s, SUM_s;

  Add #(.Bits(24)) SUM (.a(pc[23:0]), .b(24'h1), .c_i(1'b0), .s(SUM_s));  // open: c_o
  Add #(.Bits(24)) SUM_2 (.a(pc[23:0]), .b(24'h2), .c_i(1'b0), .s(SUM_2_s));  // open: c_o
  Add #(.Bits(24)) SUM_3 (.a(pc[23:0]), .b(24'h3), .c_i(1'b0), .s(SUM_3_s));  // open: c_o
  ROM #(.bigEndian("true"), .AddrBits(24), .Bits(8)) Mx0 (.A(pc[23:0]), .sel(1'b1), .D(out[31:24]));
  ROM #(.bigEndian("true"), .AddrBits(24), .Bits(8)) Mx1 (.A(SUM_s), .sel(1'b1), .D(out[23:16]));
  ROM #(.bigEndian("true"), .AddrBits(24), .Bits(8)) Mx2 (.A(SUM_2_s), .sel(1'b1), .D(out[15:8]));
  ROM #(.bigEndian("true"), .AddrBits(24), .Bits(8)) Mx3 (.A(SUM_3_s), .sel(1'b1), .D(out[7:0]));

  // Notes on the sheet:
  //   contents of Mx0 (hex, n*v repeats v):
  //   0,31,0,b3
  //   contents of Mx1 (hex, n*v repeats v):
  //   0,31,0,b3
  //   contents of Mx2 (hex, n*v repeats v):
  //   0,31,0,b3
  //   contents of Mx3 (hex, n*v repeats v):
  //   0,31,0,b3
endmodule
