// Digital circuit JType.dig as structural Verilog
module JType (
  input  [24:0] inst,
  output [31:0] imm32
);

  // Probe on inst
  BitExtender #(.inputBits(21), .outputBits(32)) bitextender_1 (
    .in({inst[24], inst[12:5], inst[13], inst[23:14], 1'b0}), .out(imm32));
  // Probe on {inst[24], inst[12:5], inst[13], inst[23:14], 1'b0}
  // Probe on imm32
endmodule
