// Digital circuit SType.dig as structural Verilog
module SType (
  input  [24:0] inst,
  output [31:0] imm32
);

  BitExtender #(.inputBits(12), .outputBits(32)) bitextender_1 (.in({inst[24:18], inst[4:0]}), .out(imm32));
endmodule
