// Digital circuit UType.dig as structural Verilog
module UType (
  input  [24:0] inst,
  output [31:0] imm32
);

  wire [31:0] bitextender_1_out;

  BitExtender #(.inputBits(20), .outputBits(32)) bitextender_1 (.in(inst[24:5]), .out(bitextender_1_out));
  // Probe on inst[24:5]
  BarrelShifter #(.Bits(32)) barrelshifter_1 (.in(bitextender_1_out), .shift(6'b001100), .out(imm32));
  // Probe on imm32
endmodule
