// Digital circuit VGA.dig as structural Verilog
module VGA (
  input  RamClock,
  input  [15:0] D_in,
  input  str,
  input  ld,
  input  [15:0] A,
  input  PixClock,
  output [15:0] D,
  output sel,
  output H_sync,
  output V_sync,
  output [11:0] Col
);

  wire and_2_out, comparator_1_eq, corev_1_p8, corev_1_p9;
  wire [11:0] corev_1_p10;

  Comparator #(.Bits(4)) comparator_1 (.a(4'b1000), .b(A[15:12]), .eq(comparator_1_eq));  // open: gt, lt
  and and_1 (sel, ld, comparator_1_eq);
  and and_2 (and_2_out, str, comparator_1_eq);
  // coreV corev_1: pin names not known; wires that end beside it: sel, and_2_out, A[11:0], D_in, RamClock, PixClock, D, corev_1_p8, corev_1_p9, corev_1_p10
  D_FF d_ff_1 (.D(corev_1_p8), .C(PixClock), .Q(H_sync));  // open: nQ
  D_FF d_ff_2 (.D(corev_1_p9), .C(PixClock), .Q(V_sync));  // open: nQ
  D_FF #(.Bits(12)) d_ff_3 (.D(corev_1_p10), .C(PixClock), .Q(Col));  // open: nQ

  // Notes on the sheet:
  //   RamClock: Hz: 25000000
  //   PixClock: Hz: 25000000
endmodule
