// Digital circuit c.dig as structural Verilog
module c (
  input  En,
  input  clk,
  output Cout,
  output [3:0] Out
);

  wire and_1_out, and_2_out, and_3_out, xor_1_out, xor_2_out, xor_3_out, xor_4_out;

  and and_1 (and_1_out, Out[0], En);
  and and_2 (and_2_out, Out[1], and_1_out);
  xor xor_1 (xor_1_out, Out[0], En);
  xor xor_2 (xor_2_out, Out[1], and_1_out);
  and and_3 (and_3_out, Out[2], and_2_out);
  and and_4 (Cout, Out[3], and_3_out);
  xor xor_3 (xor_3_out, Out[2], and_2_out);
  xor xor_4 (xor_4_out, Out[3], and_3_out);
  D_FF d_ff_1 (.D(xor_1_out), .C(clk), .Q(Out[0]));  // open: nQ
  D_FF d_ff_2 (.D(xor_2_out), .C(clk), .Q(Out[1]));  // open: nQ
  D_FF d_ff_3 (.D(xor_3_out), .C(clk), .Q(Out[2]));  // open: nQ
  D_FF d_ff_4 (.D(xor_4_out), .C(clk), .Q(Out[3]));  // open: nQ
endmodule
