// Digital circuit core-vga.dig as structural Verilog
module core_vga (
  input  clk,
  input  [31:0] pc
);

  wire char, comparator_1_eq, sync_1_p2, sync_1_p3;
  wire [6:0] ScreenRam_d;

  VGA vga_1 ();  // open: RamClock, D_in, str, ld, A, PixClock, D, sel, H_sync, V_sync, Col
  ROM #(.AddrBits(12), .Bits(7)) ScreenRam (.sel(1'b1), .D(ScreenRam_d));  // open: A
  // sync sync_1: pin names not known; wires that end beside it: clk, sync_1_p2, sync_1_p3
  Comparator #(.Bits(12)) comparator_1 (.a({12{1'b0}}), .eq(comparator_1_eq));  // open: b, gt, lt
  Multiplexer multiplexer_1 (.sel(comparator_1_eq), .in_0(ScreenRam_d[0]), .in_1(pc[0]), .out(char));
  // textMode textmode_1: pin names not known; wires that end beside it: char, clk, sync_1_p3, sync_1_p2
  VGA vga_2 (.C(clk));  // open: R, G, B, H, V
  // Pins of 1 and 7 bits meet at ScreenRam_d
  // Pins of 1 and 32 bits meet at pc
endmodule
