// Digital circuit core.dig as structural Verilog
module core (
  input  clk
);

  wire AluASrc, AluBSrc, branch_1_out, RdWr;
  wire [1:0] RdDataWr;
  wire [2:0] Funct3, ImmOp;
  wire [3:0] AluOp, BranchOp, MemoOp;
  wire [4:0] rd, rs1, rs2;
  wire [6:0] Funct7, Opcode;
  wire [31:0] add_1_s, AluOut, data_memory_1_datard, DataWr, immgenerator_1_imm, multiplexer_1_out,
       multiplexer_2_out, multiplexer_3_out, pc_1_out, register_unit_1_rs1data, register_unit_1_rs2data;

  PC pc_1 (.in(multiplexer_3_out), .clk(clk), .out(pc_1_out));
  Add #(.Bits(32)) add_1 (.a(pc_1_out), .b(32'h4), .c_i(1'b0), .s(add_1_s));  // open: c_o
  Insts_Memory insts_memory_1 (.pc(pc_1_out), .out({Funct7, rs2, rs1, Funct3, rd, Opcode}));
  // Probe on pc_1_out
  // Probe on {Funct7, rs2, rs1, Funct3, rd, Opcode}
  ControlUnit controlunit_1 (
    .opcode(Opcode), .funct3(Funct3), .funct7(Funct7), .alu_op(AluOp), .AluBSrc(AluBSrc), .immOp(ImmOp),
    .BranchOp(BranchOp), .need_write(RdWr), .memoOp(MemoOp), .AluASrc(AluASrc), .RdDataWr(RdDataWr));
  // Probe on ImmOp
  ImmGenerator immgenerator_1 (.inst({Funct7, rs2, rs1, Funct3, rd}), .ImmOp(ImmOp), .imm(immgenerator_1_imm));
  register_unit register_unit_1 (
    .rdData(DataWr), .rs1(rs1), .rs2(rs2), .rd(rd), .clk(clk), .enable(RdWr),
    .rs1Data(register_unit_1_rs1data), .rs2Data(register_unit_1_rs2data));
  // Probe on register_unit_1_rs2data
  Multiplexer #(.Bits(32)) multiplexer_1 (
    .sel(AluASrc), .in_0(pc_1_out), .in_1(register_unit_1_rs1data), .out(multiplexer_1_out));
  Multiplexer #(.Bits(32)) multiplexer_2 (
    .sel(AluBSrc), .in_0(register_unit_1_rs2data), .in_1(immgenerator_1_imm), .out(multiplexer_2_out));
  Branch branch_1 (.rs1(register_unit_1_rs1data), .rs2(register_unit_1_rs2data), .BrOp(BranchOp), .out(branch_1_out));
  // ALU alu_1: pin names not known; wires that end beside it: multiplexer_1_out, multiplexer_2_out, AluOp, AluOut
  // Probe on AluOp
  Multiplexer #(.Bits(32)) multiplexer_3 (.sel(branch_1_out), .in_0(add_1_s), .in_1(AluOut), .out(multiplexer_3_out));
  // Probe on immgenerator_1_imm
  // Probe on immgenerator_1_imm
  // Probe on AluOut
  data_memory data_memory_1 (
    .adress(AluOut), .rs(register_unit_1_rs2data), .memoOp(MemoOp), .clk(clk), .dataRd(data_memory_1_datard));
  // Probe on data_memory_1_datard
  Multiplexer #(.Selector_Bits(2), .Bits(32)) multiplexer_4 (
    .sel(RdDataWr), .in_0(add_1_s), .in_1(data_memory_1_datard), .in_2(AluOut), .in_3(immgenerator_1_imm),
    .out(DataWr));
  // Probe on DataWr
endmodule
