// Digital circuit data_memory.dig as structural Verilog
module data_memory (
  input  [31:0] adress,
  input  [31:0] rs,
  input  [3:0] memoOp,
  input  clk,
  output [31:0] dataRd
);

  wire comparator_1_eq, comparator_2_eq, comparator_3_eq, comparator_4_eq, comparator_5_eq, comparator_6_eq,
       not_1_out, not_2_out, not_3_out, not_4_out, or_1_out, or_2_out, or_3_out, w_ram1_2, w_ram3_4, w_ram4;
  wire [7:0] ram1, ram2, ram3;
  wire [31:0] lb, lh, lw_lhu_lbu;

  Comparator #(.Bits(3)) comparator_1 (.a(memoOp[2:0]), .b(3'b010), .eq(comparator_1_eq));  // open: gt, lt
  Comparator #(.Bits(3)) comparator_2 (.a(memoOp[2:0]), .b(3'b010), .eq(comparator_2_eq));  // open: gt, lt
  RAMDualPort #(.AddrBits(24), .Bits(8)) _1 (
    .A(adress[23:0]), .Din(rs[31:24]), .str(w_ram1_2), .C(clk), .ld(not_1_out), .D(ram1));
  not not_1 (not_1_out, memoOp[3]);
  Multiplexer #(.Bits(8)) multiplexer_1 (.sel(comparator_1_eq), .in_0({8{1'b0}}), .in_1(ram1), .out(lw_lhu_lbu[31:24]));
  and and_1 (w_ram1_2, memoOp[3], comparator_2_eq);
  not not_2 (not_2_out, memoOp[3]);
  RAMDualPort #(.AddrBits(24), .Bits(8)) _2 (
    .A(adress[23:0]), .Din(rs[23:16]), .str(w_ram1_2), .C(clk), .ld(not_2_out), .D(ram2));
  Multiplexer #(.Bits(8)) multiplexer_2 (.sel(comparator_1_eq), .in_0({8{1'b0}}), .in_1(ram2), .out(lw_lhu_lbu[23:16]));
  Comparator #(.Bits(3)) comparator_3 (.a(memoOp[2:0]), .b(3'b001), .eq(comparator_3_eq));  // open: gt, lt
  Comparator #(.Bits(3)) comparator_4 (.a(memoOp[2:0]), .b(3'b001), .eq(comparator_4_eq));  // open: gt, lt
  Comparator #(.Bits(3)) comparator_5 (.a(memoOp[2:0]), .b(3'b101), .eq(comparator_5_eq));  // open: gt, lt
  or or_1 (or_1_out, w_ram3_4, w_ram1_2);
  or or_2 (or_2_out, comparator_4_eq, comparator_1_eq, comparator_5_eq);
  and and_2 (w_ram3_4, memoOp[3], comparator_3_eq);
  Multiplexer #(.Bits(8)) multiplexer_3 (.sel(or_2_out), .in_0({8{1'b0}}), .in_1(ram3), .out(lw_lhu_lbu[15:8]));
  RAMDualPort #(.AddrBits(24), .Bits(8)) _3 (
    .A(adress[23:0]), .Din(rs[15:8]), .str(or_1_out), .C(clk), .ld(not_3_out), .D(ram3));
  not not_3 (not_3_out, memoOp[3]);
  Comparator #(.Bits(3)) comparator_6 (.a(memoOp[2:0]), .b(3'b000), .eq(comparator_6_eq));  // open: gt, lt
  BitExtender #(.outputBits(32)) bitextender_1 (.in(lw_lhu_lbu[7:0]), .out(lb));
  BitExtender #(.inputBits(16), .outputBits(32)) bitextender_2 (.in(lw_lhu_lbu[15:0]), .out(lh));
  and and_3 (w_ram4, memoOp[3], comparator_6_eq);
  or or_3 (or_3_out, w_ram3_4, w_ram1_2, w_ram4);
  not not_4 (not_4_out, memoOp[3]);
  RAMDualPort #(.AddrBits(24), .Bits(8)) _4 (
    .A(adress[23:0]), .Din(rs[7:0]), .str(or_3_out), .C(clk), .ld(not_4_out), .D(lw_lhu_lbu[7:0]));
  Multiplexer #(.Bits(32), .Selector_Bits(3)) multiplexer_4 (
    .sel(memoOp[2:0]), .in_0(lb), .in_1(lh), .in_2(lw_lhu_lbu), .in_3({32{1'b0}}), .in_4(lw_lhu_lbu),
    .in_5(lw_lhu_lbu), .in_6({32{1'b0}}), .in_7({32{1'b0}}), .out(dataRd));

  // Other names for the same wires on the sheet: adress_t[23:0] = adress[23:0]; funct3[2:0] = memoOp[2:0];
  //   s = memoOp[3]; primeros8[7:0] = lw_lhu_lbu[31:24]; w_ultimos8[7:0] = rs[7:0]; w_terceros8[7:0] = rs[15:8];
  //   w_segundos8[7:0] = rs[23:16]; w_primeros8[7:0] = rs[31:24]; segundos8[7:0] = lw_lhu_lbu[23:16];
  //   terceros8[7:0] = lw_lhu_lbu[15:8]; ultimos8[7:0] = lw_lhu_lbu[7:0]
endmodule
