// Digital circuit register unity.dig as structural Verilog
module register_unity (
  input  [31:0] instr,
  input  write
);

  EEPROM #(.Bits(8)) x0__0_7 (.CS(1'b1));  // open: A, WE, OE, D
  EEPROM #(.Bits(8)) x0__8_15 (.CS(1'b1));  // open: A, WE, OE, D
  EEPROM #(.Bits(8)) x0__16_23 (.CS(1'b1));  // open: A, WE, OE, D
  EEPROM #(.Bits(8)) x0__24_31 (.CS(1'b1));  // open: A, WE, OE, D

  // Other names for the same wires on the sheet: opcode[6:0] = instr[6:0]; resto[24:0] = instr[31:7]
endmodule
