// Digital circuit register_unit.dig as structural Verilog
module register_unit (
  input  [31:0] rdData,
  input  [4:0] rs1,
  input  [4:0] rs2,
  input  [4:0] rd,
  input  clk,
  input  enable,
  output [31:0] rs1Data,
  output [31:0] rs2Data
);

  wire comparator_1_eq, multiplexer_1_out;

  Comparator #(.Bits(5)) comparator_1 (.a({5{1'b0}}), .b(rd), .eq(comparator_1_eq));  // open: gt, lt
  Multiplexer multiplexer_1 (.sel(comparator_1_eq), .in_0(enable), .in_1(1'b0), .out(multiplexer_1_out));
  RegisterFile #(.AddrBits(5), .Bits(32)) registerfile_1 (
    .Din(rdData), .we(multiplexer_1_out), .Rw(rd), .C(clk), .Ra(rs1), .Rb(rs2), .Da(rs1Data), .Db(rs2Data));
endmodule
